# Fritzing sketch schema_electrique_Robot_Grp12 (saved by Fritzing 0.9.3b)
breadboards: 1

parts:
  Mod1 = Raspberry Pi 4B
  IC1 = L293D [package=THT]
  M1 = DC Motor
  M2 = DC Motor
  JP1_GND = Header 5 [package=1x05-1mm-ra]
  JP2_5V = Header 5 [package=1x05-1mm-ra]
  TCRT1_DEVANT_GAUCHE = TCRT5000 sensor module [part_number=151608]
  TCRT1_DEVANT_DROITE = TCRT5000 sensor module [part_number=151608]
  TCRT1_IIC3_GAUCHE = TCRT5000 sensor module [part_number=151608]
  TCRT1 = TCRT5000 sensor module [part_number=151608]
  Part3 = Adafruit TCS34725 RGB Color Sensor [part_number="Adafruit #1334"]
  LCM1602_IIC1 = LCM1602 IIC [part_number="LCM1602 IIC" chip_label="LCM1602 IIC" package="DIP (Dual Inline) [THT]"]
  SG1 = Buzzer 12mm [package=buzzer-12mm]
  BAT1_4_15_V = Battery Holders [package=battery-aa]
  BAT2_4_15_V = Battery Holders [package=battery-aa]
  S1 = SWITCH-MOMENTARY-2 [package=reed_switch_pth]
  JP1_SDA = Header 3 [package=1x03-1mm-ra]
  JP1_SCL = Header 3 [package=1x03-1mm-ra]
  JP1_GND_2 = Header 3 [package=1x03-1mm-ra]

nets:
  3V3: Mod1.3V3, Part3.VIN
  5V: Mod1.5V, JP2_5V.1, LCM1602_IIC1.VCC
  N1: Mod1.GPIO2, JP1_SDA.1
  N2: Mod1.GPIO3, JP1_SCL.1
  N3: Mod1.GND, IC1.0V, JP1_GND.1, SG1.2, BAT1_4_15_V.-, JP1_GND_2.1
  N4: Mod1.GPIO17, IC1.In_3
  N5: Mod1.GPIO18, IC1.In_2
  N6: Mod1.GPIO22, TCRT1_DEVANT_GAUCHE.T+
  N7: Mod1.GPIO24, TCRT1_DEVANT_DROITE.T+
  N8: Mod1.GPIO25, SG1.1
  N9: Mod1.GPIO5, TCRT1_IIC3_GAUCHE.T+
  N10: Mod1.GPIO6, IC1.In_1
  N11: Mod1.GPIO12, IC1.Enable_1
  N12: Mod1.GPIO13, IC1.Enable_2
  N13: Mod1.GPIO19, TCRT1.T+
  N14: Mod1.GPIO16, IC1.In_4
  N15: IC1.Out_1_(_Controlled_by_Enable_1_), M1.pin_1
  N16: IC1.Out_2_(_Controlled_by_Enable_1_), M1.pin_2
  N17: IC1.+Vmotor, S1.2
  N18: IC1.Out_3_(_Controlled_by_Enable_2_), M2.pin_1
  N19: IC1.Out_4_(_Controlled_by_Enable_2_), M2.pin_2
  N20: JP1_GND.2, TCRT1_DEVANT_GAUCHE.D+
  N21: JP1_GND.3, TCRT1_DEVANT_DROITE.D+
  N22: JP1_GND.4, TCRT1_IIC3_GAUCHE.D+
  N23: JP1_GND.5, TCRT1.D+
  N24: JP2_5V.2, TCRT1_DEVANT_GAUCHE.D-
  N25: JP2_5V.3, TCRT1_DEVANT_DROITE.D-
  N26: JP2_5V.4, TCRT1_IIC3_GAUCHE.D-
  N27: JP2_5V.5, TCRT1.D-
  N28: Part3.GND, JP1_GND_2.2
  N29: Part3.SCL, JP1_SCL.2
  N30: Part3.SDA, JP1_SDA.2
  N31: LCM1602_IIC1.GND, JP1_GND_2.3
  N32: LCM1602_IIC1.SDA, JP1_SDA.3
  N33: LCM1602_IIC1.SCL, JP1_SCL.3
  N34: BAT1_4_15_V.+, BAT2_4_15_V.-
  N35: BAT2_4_15_V.+, S1.1

custom parts:
  TCRT5000 sensor module: breakout board with TCRT5000
  Adafruit TCS34725 RGB Color Sensor: Your electronics can now see in dazzling color with this lovely color light sensor. We found the best color sensor on the market, the TCS34725, which has RGB and Clear light sensing elements. An IR blocking filter, integrated on-chip and localized to the color sensing photodiodes, minimizes the IR spectral component of the incoming light and allows color measurements to be made accurately. The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
  LCM1602 IIC: I2C-Module to use a 1602 or 2004 LCD on with the wire.h libory Serial LCD Modul
